// Logisim project PIC16F84A.circ as structural Verilog: 10 circuits, main circuit PIC16F84A
// PIC\n16F84A
module PIC16F84A (
  input  RA0,
  input  RA1,
  input  RA2,
  input  RA3,
  input  RA4,
  input  RB0,
  input  RB1,
  input  RB2,
  input  RB3,
  input  RB4,
  input  RB5,
  input  RB6,
  input  RB7,
  input  OSC1_CLKIN,
  input  MCLR,
  output [12:0] PC,
  output [2:0] SW,
  output [4:0] RA4_0_out,
  output [7:0] RB7_0_out,
  output OSC2_CLKOUT,
  output [7:0] W_reg
);

  wire acc_w, alu_1_destf, and_1_out, clrwdt, comparator_1_eq, EEIF, instruction_decode_1_instr_w,
       instruction_reg_1_skip_o, \int , not_1_out, not_2_out, not_3_out, pop, pop_t, push, push_t, RAM_w,
       result_w, skip, sleep, WDT, wdt_t;
  wire [0:0] CLK_RST;
  wire [1:0] instruction_decode_1_step;
  wire [2:0] stack_counter_1_stack_pointer;
  wire [4:0] jumps;
  wire [5:3] instruction_reg_1_instr_out_2;
  wire [6:0] control, multiplexer_1_out;
  wire [7:0] alu_1_output, controlled_buffer_1_out, FSR_reg, INTCON, multiplexer_2_out, OPT,
       ram_1_data_bus_out, register_2_q, SW_IN, TMR0;
  wire [8:0] timing_1_rate_2;
  wire [9:0] watchdog_1_wdt_timer;
  wire [10:0] instruction_reg_1_instr_out;
  wire [12:0] PCL_LATH, stack_counter_1_data_out;
  wire [13:0] rom_1_data;
  wire [15:0] ROM_in;
  wire [15:11] SFR_out;
  wire [23:0] ROM_out;

  and and_1 (and_1_out, result_w, skip);
  // Probe on instruction_reg_1_skip_o
  Instruction_reg instruction_reg_1 (
    .instr_w(instruction_decode_1_instr_w),
    .Instr_OUT({instruction_reg_1_instr_out_2, instruction_reg_1_instr_out}), .Instr_IN(rom_1_data),
    .CLK_RST({MCLR, CLK_RST[0]}), .SKIP_o(instruction_reg_1_skip_o), .Skip(and_1_out));
  Clock clock_1 (.out(CLK_RST[0]));
  // Probe on rom_1_data
  // Probe on {instruction_reg_1_instr_out_2, instruction_reg_1_instr_out}
  Instruction_decode instruction_decode_1 (
    .CLK_RST({MCLR, CLK_RST[0]}), .OPCODE({instruction_reg_1_instr_out_2, instruction_reg_1_instr_out}),
    .STEP(instruction_decode_1_step), .instr_w(instruction_decode_1_instr_w), .carry(OSC2_CLKOUT),
    .result_w(result_w), .reg_w(control[1]), .push(push), .pop(pop), .egie(control[2]), .clrwdt(clrwdt),
    .sleep(sleep), .INT(\int ), .jumps(jumps));
  // Probe on instruction_decode_1_step
  // Probe on PC
  ROM #(.addrWidth(13), .dataWidth(14)) rom_1 (.addr(PC), .data(rom_1_data));  // open: sel
  Button button_1 ();  // open: out
  Program_counter program_counter_1 (
    .PROGRAM_COUNTER(PC), .CLK_RST({MCLR, CLK_RST[0]}), .SEQ(OSC2_CLKOUT), .Jump_cmd(jumps),
    .STACK(stack_counter_1_data_out), .INT(13'h4), .PCL_PCLATH(PCL_LATH), .GOTO(instruction_reg_1_instr_out));
  // Probe on instruction_reg_1_instr_out
  Stack_counter stack_counter_1 (
    .PUSH(push_t), .POP(pop_t), .Stack_pointer(stack_counter_1_stack_pointer), .DATA_IN(PC),
    .DATA_OUT(stack_counter_1_data_out), .CLK_RST({MCLR, CLK_RST[0]}));
  Watchdog watchdog_1 (
    .wdt(wdt_t), .CLRWDT_SLEEP({clrwdt, sleep}), .PD_TO(SW_IN[4:3]), .WDT_CLK(WDT),
    .WDT_TIMER(watchdog_1_wdt_timer));
  // Probe on watchdog_1_wdt_timer
  // Probe on 13'h4
  // Probe on stack_counter_1_data_out
  // Probe on stack_counter_1_stack_pointer
  // Probe on nothing
  // Probe on PCL_LATH
  Interrupt interrupt_1 (.INT(\int ), .EEIF(EEIF), .INTCON_in(INTCON));
  // Probe on INTCON
  // Probe on INTCON
  // Probe on SFR_out[13]
  // Probe on jumps[0]
  // Probe on alu_1_destf
  not not_1 (not_1_out, alu_1_destf);
  and and_2 (acc_w, not_1_out, control[1]);
  and and_3 (RAM_w, alu_1_destf, control[1]);
  not not_2 (not_2_out, instruction_reg_1_instr_out_2[5]);
  // Probe on instruction_reg_1_instr_out[7]
  // Probe on {instruction_reg_1_instr_out_2, instruction_reg_1_instr_out[10:8]}
  // Probe on register_2_q
  Comparator #(.width(7)) comparator_1 (
    .a({7{1'b0}}), .b(instruction_reg_1_instr_out[6:0]), .eq(comparator_1_eq));  // open: gt, lt
  // Probe on W_reg
  // Probe on SW
  Register register_1 (.D(register_2_q), .en(acc_w), .Q(W_reg), .clk(CLK_RST[0]), .clr(MCLR));
  // Probe on ram_1_data_bus_out
  RAM ram_1 (
    .DATA_BUS_OUT(ram_1_data_bus_out), .PC(PCL_LATH), .EEPROM_out({ROM_out[23:21], EEIF, ROM_out[19:0]}),
    .SFR_out({OPT, INTCON, SFR_out, SW, FSR_reg}), .Control_in({control[6:4], RB0, control[2:0]}),
    .EEPROM_in(ROM_in), .IO_in({RB7, RB6, RB5, RB4, RB3, RB2, RB1, RB0, RA4, RA3, RA2, RA1, RA0}),
    .SW_in(SW_IN), .WE(RAM_w), .CLK_RST({MCLR, CLK_RST[0]}), .ADDRESS(multiplexer_1_out),
    .DATA_BUS(controlled_buffer_1_out), .TMR0_IO_INT({RB7_0_out, RA4_0_out, TMR0}));
  // Probe on multiplexer_1_out
  Multiplexer #(.width(7), .enable("false")) multiplexer_1 (
    .in0(instruction_reg_1_instr_out[6:0]), .in1(FSR_reg[6:0]), .out(multiplexer_1_out), .sel(comparator_1_eq));
  // Probe on instruction_reg_1_instr_out[6:0]
  // Probe on FSR_reg[6:0]
  // Probe on controlled_buffer_1_out
  // Probe on instruction_reg_1_instr_out[7:0]
  // Probe on not_2_out
  Multiplexer #(.width(8), .enable("false")) multiplexer_2 (
    .in0(instruction_reg_1_instr_out[7:0]), .in1(controlled_buffer_1_out), .out(multiplexer_2_out),
    .sel(not_2_out));
  // Probe on multiplexer_2_out
  // Probe on SW_IN[2:0]
  ALU alu_1 (
    .Z_DC_C(SW), .DATA(multiplexer_2_out), .W(W_reg), .OP_7(instruction_reg_1_instr_out[7]),
    .SEL({instruction_reg_1_instr_out_2, instruction_reg_1_instr_out[10:8]}), .destf(alu_1_destf),
    .Skip(skip), .sw_w(SW_IN[5]), .Z_DC_C_out(SW_IN[2:0]), .OUTPUT(alu_1_output));  // open: Control, Call_Goto
  // Probe on SW_IN[5]
  // Probe on alu_1_output
  not not_3 (not_3_out, RAM_w);
  assign controlled_buffer_1_out = not_3_out ? ram_1_data_bus_out : 8'bz;  // Controlled_Buffer controlled_buffer_1
  // Probe on {SFR_out, SW}
  Register #(.trigger("falling")) register_2 (
    .D(alu_1_output), .en(result_w), .Q(register_2_q), .clk(CLK_RST[0]), .clr(MCLR));
  assign controlled_buffer_1_out = RAM_w ? register_2_q : 8'bz;  // Controlled_Buffer controlled_buffer_2
  // Probe on controlled_buffer_1_out
  // Probe on ROM_out[7:0]
  // Probe on controlled_buffer_1_out
  // Probe on ROM_in[7:0]
  EEPROM eeprom_1 (
    .EEDATA(ROM_out[7:0]), .EEADR(ROM_out[15:8]), .EECON1_out(ROM_in[15:8]),
    .EECON1({ROM_out[23:21], EEIF, ROM_out[19:16]}), .CLK_RST({MCLR, CLK_RST[0]}), .EEDATA_out(ROM_in[7:0]),
    .EE_W(control[6:4]));
  // Probe on ROM_out[15:8]
  // Probe on TMR0
  Timing timing_1 (
    .SEQ(OSC2_CLKOUT), .T0CLK(RA4), .RST(MCLR), .WDT(WDT), .rate(control[0]), .wdt_2(wdt_t), .OPT(OPT),
    .rate_2(timing_1_rate_2));
  // Probe on timing_1_rate_2
  // Probe on OPT
  // Probe on ROM_in[15:8]
  // Probe on {ROM_out[23:21], EEIF, ROM_out[19:16]}
  Clock #(.highDuration(2), .lowDuration(2)) clock_2 ();  // open: out
  // Probe on RA4

  // Other names for the same wires on the sheet: CLK_RST[1] = MCLR; rst = MCLR; tmr_w = control[0];
  //   reg_w = control[1]; egie = control[2]; EE_W[2:0] = control[6:4];
  //   IO_in[12:0] = {RB7, RB6, RB5, RB4, RB3, RB2, RB1, RB0, RA4, RA3, RA2, RA1, RA0}; control[3] = RB0; INTF = RB0;
  //   ROM_out[20] = EEIF; SEQ = OSC2_CLKOUT; SFR_out (some bits) = {OPT, INTCON, SW, FSR_reg};
  //   SW_t[7:0] = {SFR_out, SW}; TMR0_IO[20:0] = {RB7_0_out, RA4_0_out, TMR0}; PORTA_out[4:0] = RA4_0_out;
  //   PORTB_out[7:0] = RB7_0_out

  // Notes on the sheet:
  //   1K x 14
  //   Instruction
  //    Decode 
  //   & Control  
  //   Timing
  //   Flash Program
  //   Instruction reg
  //   contents of rom_1 (hex, n*v repeats v):
  //   0 2850 0 280d 9f e03 9e 2017 e03 83 e9f e1f 9 0 1683 1786 1283 3088 8b 1585 1185 0 2815 0 1683 307f
  //   86 1283 3004 9c 3018 84 0 1485 1085 100 806 1803 2829 80 a84 b9c 2820 3012 9d 3018 84 3048 880 1c03
  //   283b a84 3069 880 1c03 283b a84 300c 9d 0 1683 3080 86 1283 81d 84 3006 9c 800 86 1505 1105 a84 b9c
  //   2844 1585 1185 1386 100b 3400 0 3048 8c 3065 8d 306c 8e 306c 8f 306f 90 300a 91 3062 92 3069 93 3073
  //   94 306f 95 3075 96 300a 97 3000 98 3000 99 3000 9a 3000 9b 2802
  //   Program counter
  //   8 level stack
  //   Control and signals
  //   Watchdog
  //   Program counter, branching
  //   Interruptor
  //   INDF
  //   ALU
  //   ALU
  //   RAM
  //   RAM File 
  //   Registers
  //   68 x 8
  //   EEPROM
  //   EEPROM
  //   64x8
  //   TMR0
  //   IO ports
endmodule

module Program_counter (
  input  [4:0] Jump_cmd,
  input  [1:0] CLK_RST,
  input  SEQ,
  input  [12:0] PCL_PCLATH,
  input  [12:0] STACK,
  input  [10:0] GOTO,
  input  [12:0] INT,
  output [12:0] PROGRAM_COUNTER
);

  wire and_1_out, not_1_out;
  wire [1:0] priority_encoder_1_out;
  wire [12:0] multiplexer_1_out;

  // Probe on Jump_cmd[0]
  // Probe on Jump_cmd[4]
  // Probe on Jump_cmd[3]
  // Probe on Jump_cmd[2]
  // Probe on Jump_cmd[1]
  Priority_Encoder #(.select(2)) priority_encoder_1 (
    .in0(Jump_cmd[4]), .in1(Jump_cmd[3]), .in2(Jump_cmd[2]), .in3(Jump_cmd[1]), .out(priority_encoder_1_out));  // open: gs, en_out, en_in
  // Probe on PCL_PCLATH
  // Probe on {PCL_PCLATH[12:11], GOTO}
  // Probe on Jump_cmd[0]
  not not_1 (not_1_out, Jump_cmd[0]);
  // Probe on multiplexer_1_out
  Multiplexer #(.select(2), .width(13), .enable("false")) multiplexer_1 (
    .in0(PCL_PCLATH), .in1({PCL_PCLATH[12:11], GOTO}), .in2(INT), .in3(STACK), .out(multiplexer_1_out),
    .sel(priority_encoder_1_out));
  // Probe on priority_encoder_1_out
  // Probe on multiplexer_1_out
  Counter #(.width(13), .max('h1fff)) PC (
    .load(Jump_cmd[0]), .D(multiplexer_1_out), .count(and_1_out), .Q(PROGRAM_COUNTER), .clk(CLK_RST[0]),
    .clr(CLK_RST[1]));  // open: carry
  and and_1 (and_1_out, not_1_out, SEQ);
  // Probe on STACK
  // Probe on INT
endmodule

module Stack_counter (
  input  [12:0] DATA_IN,
  input  PUSH,
  input  [1:0] CLK_RST,
  input  POP,
  output [2:0] Stack_pointer,
  output [12:0] DATA_OUT
);

  wire and_1_out, not_1_out, not_2_out, or_1_out, subtractor_1_bout;
  wire [2:0] adder_1_out, controlled_buffer_1_out, multiplexer_1_out, subtractor_1_out;

  Adder #(.width(3)) adder_1 (.a(Stack_pointer), .b({2'b00, PUSH}), .out(adder_1_out), .cin(1'b0));  // open: cout
  and and_1 (and_1_out, POP, not_1_out);
  Subtractor #(.width(3)) subtractor_1 (
    .a(Stack_pointer), .b({2'b00, POP}), .out(subtractor_1_out), .bin(1'b0), .bout(subtractor_1_bout));
  not not_1 (not_1_out, subtractor_1_bout);
  or or_1 (or_1_out, PUSH, and_1_out);
  assign controlled_buffer_1_out = PUSH ? adder_1_out : 3'bz;  // Controlled_Buffer controlled_buffer_1
  assign controlled_buffer_1_out = POP ? subtractor_1_out : 3'bz;  // Controlled_Buffer controlled_buffer_2
  Register #(.width(3)) register_1 (
    .D(controlled_buffer_1_out), .en(or_1_out), .Q(Stack_pointer), .clk(CLK_RST[0]), .clr(CLK_RST[1]));
  // Probe on Stack_pointer
  Multiplexer #(.width(3), .enable("false")) multiplexer_1 (
    .in0(Stack_pointer), .in1(adder_1_out), .out(multiplexer_1_out), .sel(PUSH));
  RAM #(.addrWidth(3), .dataWidth(13)) ram_1 (
    .addr(multiplexer_1_out), .data(DATA_OUT), .sel(1'b1), .clk(CLK_RST[0]), .ld(not_2_out), .clr(CLK_RST[1]));
  not not_2 (not_2_out, PUSH);
  assign DATA_OUT = PUSH ? DATA_IN : 13'bz;  // Controlled_Buffer controlled_buffer_3

  // Other names for the same wires on the sheet: SP[2:0] = Stack_pointer
endmodule

module Instruction_decode (
  input  [1:0] CLK_RST,
  input  INT,
  input  [13:0] OPCODE,
  output [1:0] STEP,
  output instr_w,
  output carry,
  output result_w,
  output reg_w,
  output push,
  output [4:0] jumps,
  output pop,
  output egie,
  output clrwdt,
  output sleep
);

  wire and_1_out, and_2_out, and_3_out, and_9_out, and_11_out, comparator_1_eq, comparator_2_eq,
       comparator_3_eq, comparator_4_eq, comparator_6_eq, comparator_7_eq, comparator_8_eq, decoder_1_out1,
       decoder_1_out2, not_1_out, not_2_out, not_3_out, not_4_out, not_5_out, not_6_out, not_7_out, or_3_out,
       or_4_out, or_5_out, skips;

  Counter #(.width(2), .max('h3)) counter_1 (
    .Q(STEP), .clk(CLK_RST[0]), .clr(CLK_RST[1]));  // open: load, D, count, carry
  Decoder #(.select(2), .enable("false")) decoder_1 (
    .out0(instr_w), .out1(decoder_1_out1), .out2(decoder_1_out2), .out3(carry), .sel(STEP));
  Comparator #(.width(6)) comparator_1 (.a(6'b001111), .b(OPCODE[13:8]), .eq(comparator_1_eq));  // open: gt, lt
  Comparator #(.width(6)) comparator_2 (.a(6'b001011), .b(OPCODE[13:8]), .eq(comparator_2_eq));  // open: gt, lt
  Comparator #(.width(3)) comparator_3 (.a(3'b011), .b(OPCODE[13:11]), .eq(comparator_3_eq));  // open: gt, lt
  Comparator #(.width(7)) comparator_4 (.a(OPCODE[13:7]), .b({7{1'b0}}), .eq(comparator_4_eq));  // open: gt, lt
  Comparator #(.width(2)) comparator_5 (.a(OPCODE[13:12]), .b(2'b10), .eq(jumps[3]));  // open: gt, lt
  not not_1 (not_1_out, OPCODE[11]);
  Comparator #(.width(6)) comparator_6 (.a(OPCODE[13:8]), .b(6'b110100), .eq(comparator_6_eq));  // open: gt, lt
  Comparator #(.width(11)) comparator_7 (.a(OPCODE[13:3]), .b(11'h1), .eq(comparator_7_eq));  // open: gt, lt
  Comparator #(.width(11)) comparator_8 (.a(OPCODE[13:3]), .b(11'hc), .eq(comparator_8_eq));  // open: gt, lt
  or or_1 (skips, comparator_1_eq, comparator_2_eq, comparator_3_eq);
  not not_2 (not_2_out, comparator_4_eq);
  not not_3 (not_3_out, jumps[3]);
  and and_1 (and_1_out, jumps[3], not_1_out);
  or or_2 (jumps[1], comparator_6_eq, comparator_7_eq);
  and and_2 (and_2_out, comparator_7_eq, OPCODE[0]);
  not not_4 (not_4_out, jumps[3]);
  not not_5 (not_5_out, jumps[1]);
  not not_6 (not_6_out, skips);
  and and_3 (and_3_out, not_2_out, not_3_out);
  or or_3 (or_3_out, and_1_out, jumps[2]);
  or or_4 (or_4_out, jumps[3], jumps[2]);
  or or_5 (or_5_out, jumps[2], and_2_out);
  and and_4 (jumps[2], INT, not_4_out, not_5_out, not_6_out);
  and and_5 (result_w, decoder_1_out1, and_3_out);
  and and_6 (push, decoder_1_out1, or_3_out);
  and and_7 (pop, decoder_1_out1, jumps[1]);
  and and_8 (reg_w, decoder_1_out2, and_3_out);
  and and_9 (and_9_out, carry, or_4_out);
  and and_10 (egie, carry, or_5_out);
  and and_11 (and_11_out, comparator_8_eq, carry);
  // Probe on jumps[0]
  or or_6 (jumps[0], and_9_out, pop);
  and and_12 (clrwdt, and_11_out, OPCODE[2]);
  and and_13 (sleep, and_11_out, not_7_out);
  not not_7 (not_7_out, OPCODE[2]);

  assign jumps[4] = 1'b0;

  // Other names for the same wires on the sheet: returns = jumps[1]; int_t = jumps[2]; call_goto = jumps[3]

  // Notes on the sheet:
  //   Sequencer
  //   Control
  //   returns
  //   sleep/clrwdt
  //   retlw
  //   ret,retfie
  //   call
  //   retfie
  //   returns
  //   clrwdt
  //   ALU operation
  //   call or int
  //   int or call,goto 
  //   toggle gie
  //   Sequencing
  //   0
  //   1
  //   0
  //   1
  //   2
  //   3
  //   2
  //   3
endmodule

module Instruction_reg (
  input  [13:0] Instr_IN,
  input  Skip,
  input  instr_w,
  input  [1:0] CLK_RST,
  output SKIP_o,
  output [13:0] Instr_OUT
);

  wire and_1_out, d_ff_1_qn, not_1_out;
  wire [13:0] multiplexer_1_out;

  and and_1 (and_1_out, Skip, not_1_out);
  not not_1 (not_1_out, instr_w);
  D_Flip_Flop #(.trigger("falling")) d_ff_1 (
    .clk(CLK_RST[0]), .D(not_1_out), .Q(SKIP_o), .Qn(d_ff_1_qn), .preset(and_1_out), .en(instr_w));  // open: reset
  Multiplexer #(.width(14), .disabled(0), .enable("false")) multiplexer_1 (
    .in0({14{1'b0}}), .in1(Instr_IN), .out(multiplexer_1_out), .sel(d_ff_1_qn));
  // Probe on multiplexer_1_out
  // Probe on Instr_IN
  Register #(.width(14), .trigger("falling")) register_1 (
    .D(multiplexer_1_out), .en(instr_w), .Q(Instr_OUT), .clk(CLK_RST[0]), .clr(CLK_RST[1]));
endmodule

module Interrupt (
  input  EEIF,
  input  [7:0] INTCON_in,
  output INT
);

  wire and_2_out, and_3_out, and_4_out, and_5_out, or_1_out;

  and and_1 (INT, or_1_out, INTCON_in[7]);
  or or_1 (or_1_out, and_2_out, and_3_out, and_4_out, and_5_out);
  and and_2 (and_2_out, INTCON_in[0], INTCON_in[3]);
  and and_3 (and_3_out, INTCON_in[1], INTCON_in[4]);
  and and_4 (and_4_out, INTCON_in[2], INTCON_in[5]);
  and and_5 (and_5_out, EEIF, INTCON_in[6]);
  // Probe on INTCON_in
  // Probe on INTCON_in[0]
  // Probe on INTCON_in[1]
  // Probe on INTCON_in[2]
  // Probe on EEIF

  // Notes on the sheet:
  //   Interrupt Handling
endmodule

module EEPROM (
  input  [7:0] EEDATA,
  input  [7:0] EEADR,
  input  [7:0] EECON1,
  input  [1:0] CLK_RST,
  output [7:0] EEDATA_out,
  output [2:0] EE_W,
  output [7:0] EECON1_out
);

  wire and_1_out, buffer_1_out, counter_1_carry, not_1_out, not_2_out, or_1_out;

  // Probe on EEADR
  not not_1 (not_1_out, counter_1_carry);
  or or_1 (or_1_out, EECON1[0], and_1_out);
  and and_1 (and_1_out, EECON1[2], EECON1[1]);
  // Probe on EEDATA_out
  RAM ram_1 (.addr(EEADR), .data(EEDATA_out), .sel(or_1_out), .clk(CLK_RST[0]), .ld(not_1_out), .clr(CLK_RST[1]));
  not not_2 (not_2_out, and_1_out);
  and and_2 (EE_W[1], not_2_out, EECON1[0]);
  // Probe on EE_W[1]
  // Probe on EE_W[2]
  // Probe on EE_W[0]
  assign EEDATA_out = counter_1_carry ? EEDATA : 8'bz;  // Controlled_Buffer controlled_buffer_1
  Counter #(.width(2), .max('h3)) counter_1 (
    .count(and_1_out), .carry(counter_1_carry), .clk(CLK_RST[0]), .clr(CLK_RST[1]));  // open: load, D, Q
  or or_2 (EE_W[2], EE_W[1], counter_1_carry);
  // Probe on counter_1_carry
  buf buffer_1 (buffer_1_out, EECON1[4]);
  Multiplexer #(.enable("false")) multiplexer_1 (
    .in0(counter_1_carry), .in1(buffer_1_out), .out(EE_W[0]), .sel(EE_W[1]));
  assign EECON1_out[3:2] = EECON1[3:2];  // Buffer buffer_2, 2 bits wide

  assign {EECON1_out[7:4], EECON1_out[1:0]} = {3'b000, EE_W[0], 2'b00};

  // Other names for the same wires on the sheet: WREN = EECON1[2]; WRERR = EECON1[3]; RD = EECON1[0]; WR = EECON1[1];
  //   EEIF = EECON1[4]
endmodule

module Timing (
  input  SEQ,
  input  T0CLK,
  input  [7:0] OPT,
  input  RST,
  input  WDT,
  output rate,
  output [8:0] rate_2,
  output wdt_2
);

  wire multiplexer_1_out, multiplexer_2_out, prescsaler_1_ps_ckl, xor_1_out;

  Clock #(.lowDuration(3)) clock_1 ();  // open: out
  Clock clock_2 ();  // open: out
  // Probe on OPT[3]
  // Probe on OPT[5]
  // Probe on OPT[4]
  xor xor_1 (xor_1_out, T0CLK, OPT[4]);
  // Probe on OPT[4]
  Multiplexer #(.enable("false")) multiplexer_1 (.in0(SEQ), .in1(xor_1_out), .out(multiplexer_1_out), .sel(OPT[5]));
  // Probe on OPT[5]
  // Probe on OPT[3]
  Multiplexer #(.enable("false")) multiplexer_2 (
    .in0(multiplexer_1_out), .in1(WDT), .out(multiplexer_2_out), .sel(OPT[3]));
  // Probe on OPT[2:0]
  Prescsaler prescsaler_1 (
    .PS(OPT[2:0]), .CLK(multiplexer_2_out), .ps_ckl(prescsaler_1_ps_ckl), .PSA(OPT[3]), .rate(rate_2),
    .RST(RST));
  // Probe on rate_2
  Multiplexer #(.enable("false")) multiplexer_3 (
    .in0(prescsaler_1_ps_ckl), .in1(multiplexer_1_out), .out(rate), .sel(OPT[3]));
  Multiplexer #(.enable("false")) multiplexer_4 (.in0(WDT), .in1(prescsaler_1_ps_ckl), .out(wdt_2), .sel(OPT[3]));

  // Notes on the sheet:
  //   PRESCALER
endmodule

module Watchdog (
  input  wdt,
  input  [1:0] CLRWDT_SLEEP,
  output [1:0] PD_TO,
  output [9:0] WDT_TIMER,
  output WDT_CLK
);

  wire button_1_out, button_2_out, counter_1_carry, not_1_out, or_1_out;

  // Probe on CLRWDT_SLEEP[1]
  // Probe on CLRWDT_SLEEP[0]
  D_Flip_Flop d_ff_1 (.Qn(PD_TO[0]), .preset(CLRWDT_SLEEP[0]), .reset(or_1_out));  // open: clk, D, Q, en
  // Probe on PD_TO[0]
  or or_1 (or_1_out, CLRWDT_SLEEP[1], not_1_out);
  Button button_1 (.out(button_1_out));
  Button button_2 (.out(button_2_out));
  // Probe on PD_TO[1]
  or or_2 (PD_TO[1], CLRWDT_SLEEP[1], CLRWDT_SLEEP[0], not_1_out);
  Clock #(.highDuration(4), .lowDuration(4)) u_WDT (.out(WDT_CLK));
  not not_1 (not_1_out, counter_1_carry);
  Counter #(.width(10), .max('h3ff), .trigger("falling")) counter_1 (
    .load(1'b0), .count(wdt), .Q(WDT_TIMER), .carry(counter_1_carry), .clk(WDT_CLK), .clr(CLRWDT_SLEEP[1]));  // open: D
endmodule

module Prescsaler (
  input  [2:0] PS,
  input  PSA,
  input  CLK,
  input  RST,
  output ps_ckl,
  output [8:0] rate
);

  wire comparator_1_eq, comparator_2_eq, multiplexer_3_out, not_1_out, not_2_out, subtractor_1_bout;
  wire [2:0] multiplexer_1_out, register_1_q, subtractor_1_out;
  wire [7:0] counter_1_q, multiplexer_2_out;

  Register #(.width(3)) register_1 (.D(PS), .en(not_1_out), .Q(register_1_q));  // open: clk, clr
  Subtractor #(.width(3)) subtractor_1 (
    .a(PS), .b(3'b000), .out(subtractor_1_out), .bin(PSA), .bout(subtractor_1_bout));
  not not_1 (not_1_out, comparator_1_eq);
  Comparator #(.width(3)) comparator_1 (.a(PS), .b(register_1_q), .eq(comparator_1_eq));  // open: gt, lt
  Multiplexer #(.width(3), .enable("false")) multiplexer_1 (
    .in0(PS), .in1(subtractor_1_out), .out(multiplexer_1_out), .sel(PSA));
  Multiplexer #(.select(3), .width(8), .enable("false")) multiplexer_2 (
    .in0(8'h1), .in1(8'h3), .in2(8'h7), .in3(8'hf), .in4(8'h1f), .in5(8'h3f), .in6(8'h7f), .in7({8{1'b1}}),
    .out(multiplexer_2_out), .sel(multiplexer_1_out));
  Counter counter_1 (
    .load(comparator_2_eq), .D({8{1'b0}}), .count(not_2_out), .Q(counter_1_q), .clk(CLK), .clr(RST));  // open: carry
  not not_2 (not_2_out, comparator_2_eq);
  // Probe on counter_1_q
  // Probe on multiplexer_2_out
  Comparator comparator_2 (.a(counter_1_q), .b(multiplexer_2_out), .eq(comparator_2_eq));  // open: gt, lt
  and and_1 (ps_ckl, CLK, multiplexer_3_out);
  Multiplexer #(.enable("false")) multiplexer_3 (
    .in0(comparator_2_eq), .in1(CLK), .out(multiplexer_3_out), .sel(subtractor_1_bout));
  // Probe on rate
  Adder adder_1 (.a(8'h1), .b(multiplexer_2_out), .out(rate[7:0]), .cout(rate[8]));  // open: cin

  // Notes on the sheet:
  //   clk
  //   prescaler to wdt and rate=1
endmodule
