// Logisim project PIC_registers.circ as structural Verilog: 10 circuits, main circuit async_register
module tester (
);

  wire not_1_out, or_1_out, write;
  wire [1:0] button_1_out;
  wire [3:0] ram_1_timr0_ctrl_2;
  wire [4:1] control;
  wire [6:0] counter_1_q;
  wire [7:0] ram_1_data_bus_out, ram_1_timr0_ctrl;
  wire [12:0] ram_1_pc;
  wire [23:0] ram_1_eeprom_in;
  wire [31:0] ram_1_sfr_out;

  // Probe on ram_1_timr0_ctrl
  // Probe on ram_1_timr0_ctrl_2
  // Probe on ram_1_pc
  // Probe on ram_1_eeprom_in
  // Probe on ram_1_sfr_out
  Counter #(.width(7), .max('h7f)) counter_1 (
    .count(not_1_out), .Q(counter_1_q), .clk(button_1_out[0]), .clr(button_1_out[1]));  // open: load, D, carry
  not not_1 (not_1_out, or_1_out);
  or or_1 (or_1_out, control[1], control[2], control[3], write);
  Clock clock_1 (.out(button_1_out[0]));
  // Probe on ram_1_data_bus_out
  RAM ram_1 (
    .DATA_BUS_OUT(ram_1_data_bus_out), .PC(ram_1_pc), .EEPROM_in(ram_1_eeprom_in), .SFR_OUT(ram_1_sfr_out),
    .TIMR0_ctrl({ram_1_timr0_ctrl_2, ram_1_timr0_ctrl}), .Control_in({control, 1'b1}),
    .EEPROM_out({16{1'b0}}), .IO({13{1'b0}}), .SFR_IN(16'h83f0), .WE(write), .CLK_RST(button_1_out),
    .ADDRESS(counter_1_q), .DATA_BUS(ram_1_data_bus_out));
  Button button_1 (.out(button_1_out[1]));
  assign ram_1_data_bus_out = write ? 8'h4 : 8'bz;  // Controlled_Buffer controlled_buffer_1
  Button u_write (.out(write));
  // Probe on {control, 1'b1}
  Button button_2 (.out(control[1]));
  Button button_3 (.out(control[2]));
  Button button_4 (.out(control[3]));
  Button button_5 (.out(control[4]));
  // Probe on 8'hf0
  // Probe on 8'h83
  async_register async_register_1 (.WREG_CLK_RST({write, button_1_out[0], button_1_out[1]}));  // open: SYNCH_ADDRESS, DIRECT_ADDRESS, BUS_OUT, BUS_IN, AsynchronousW, OUT, WE_async
endmodule

module Stack (
  input  [12:0] DATA_IN,
  input  PUSH,
  input  [1:0] CLK_RST,
  input  POP,
  output [2:0] Stack_pointer,
  output [12:0] DATA_OUT
);

  wire and_1_out, not_1_out, not_2_out, or_1_out, subtractor_1_bout;
  wire [2:0] adder_1_out, controlled_buffer_1_out, multiplexer_1_out, subtractor_1_out;

  Adder #(.width(3)) adder_1 (.a(Stack_pointer), .b({2'b00, PUSH}), .out(adder_1_out), .cin(1'b0));  // open: cout
  and and_1 (and_1_out, POP, not_1_out);
  Subtractor #(.width(3)) subtractor_1 (
    .a(Stack_pointer), .b({2'b00, POP}), .out(subtractor_1_out), .bin(1'b0), .bout(subtractor_1_bout));
  not not_1 (not_1_out, subtractor_1_bout);
  or or_1 (or_1_out, PUSH, and_1_out);
  assign controlled_buffer_1_out = PUSH ? adder_1_out : 3'bz;  // Controlled_Buffer controlled_buffer_1
  assign controlled_buffer_1_out = POP ? subtractor_1_out : 3'bz;  // Controlled_Buffer controlled_buffer_2
  // Probe on Stack_pointer
  Register #(.width(3)) register_1 (
    .D(controlled_buffer_1_out), .en(or_1_out), .Q(Stack_pointer), .clk(CLK_RST[0]), .clr(CLK_RST[1]));
  Multiplexer #(.width(3), .enable("false")) multiplexer_1 (
    .in0(Stack_pointer), .in1(adder_1_out), .out(multiplexer_1_out), .sel(PUSH));
  RAM_part #(.addrWidth(3), .dataWidth(13)) ram_1 (
    .addr(multiplexer_1_out), .data(DATA_OUT), .sel(1'b1), .clk(CLK_RST[0]), .ld(not_2_out), .clr(CLK_RST[1]));
  not not_2 (not_2_out, PUSH);
  assign DATA_OUT = PUSH ? DATA_IN : 13'bz;  // Controlled_Buffer controlled_buffer_3

  // Other names for the same wires on the sheet: SP[2:0] = Stack_pointer
endmodule

module RAM (
  input  [7:0] DATA_BUS,
  input  [4:0] Control_in,
  input  [15:0] EEPROM_out,
  input  [12:0] IO,
  input  [15:0] SFR_IN,
  input  WE,
  input  [1:0] CLK_RST,
  input  [6:0] ADDRESS,
  output [7:0] DATA_BUS_OUT,
  output [12:0] PC,
  output [23:0] EEPROM_in,
  output [31:0] SFR_OUT,
  output [11:0] TIMR0_ctrl
);

  wire comparator_1_eq, comparator_2_eq, comparator_3_eq, not_1_out, not_2_out, not_3_out, not_4_out,
       subtractor_1_bout;
  wire [2:0] button_2_out;
  wire [6:0] multiplexer_1_out, multiplexer_2_out, subtractor_1_out;
  wire [7:0] controlled_buffer_1_out, controlled_buffer_2_out, controlled_buffer_4_out,
       controlled_buffer_5_out, EEDATA_in, porta_reg_1_out, portb_reg_1_out, TRISA, TRISB;
  wire [7:5] PCLATH;

  // Probe on DATA_BUS
  // Probe on subtractor_1_out
  // Probe on controlled_buffer_1_out
  Comparator #(.width(7)) comparator_1 (.a(ADDRESS), .b({7{1'b0}}), .eq(comparator_1_eq));  // open: gt, lt
  assign controlled_buffer_1_out = comparator_1_eq ? {8{1'b0}} : 8'bz;  // Controlled_Buffer controlled_buffer_1
  // Probe on PC[7:0]
  // Probe on SFR_OUT[15:8]
  // Probe on SFR_OUT[7:0]
  // Probe on {PCLATH, PC[12:8]}
  // Probe on SFR_OUT[23:16]
  Subtractor #(.width(7)) subtractor_1 (
    .a(ADDRESS), .b(7'b0001100), .out(subtractor_1_out), .bin(1'b0), .bout(subtractor_1_bout));
  not not_1 (not_1_out, subtractor_1_bout);
  assign DATA_BUS_OUT = controlled_buffer_1_out;  // Buffer buffer_1, 8 bits wide
  async_register async_register_1 (
    .SYNCH_ADDRESS(ADDRESS), .DIRECT_ADDRESS(7'b0000010), .BUS_OUT(DATA_BUS_OUT), .BUS_IN(DATA_BUS),
    .OUT(PC[7:0]), .WREG_CLK_RST({WE, CLK_RST}), .WE_async(1'b0));  // open: AsynchronousW
  async_register async_register_2 (
    .SYNCH_ADDRESS(ADDRESS), .DIRECT_ADDRESS(7'b0000011), .BUS_OUT(DATA_BUS_OUT), .BUS_IN(DATA_BUS),
    .AsynchronousW(SFR_IN[15:8]), .OUT(SFR_OUT[15:8]), .WREG_CLK_RST({WE, CLK_RST}), .WE_async(Control_in[1]));
  async_register async_register_3 (
    .SYNCH_ADDRESS(ADDRESS), .DIRECT_ADDRESS(7'b0000100), .BUS_OUT(DATA_BUS_OUT), .BUS_IN(DATA_BUS),
    .OUT(SFR_OUT[7:0]), .WREG_CLK_RST({WE, CLK_RST}), .WE_async(1'b0));  // open: AsynchronousW
  async_register async_register_4 (
    .SYNCH_ADDRESS(ADDRESS), .DIRECT_ADDRESS(7'b0001010), .BUS_OUT(DATA_BUS_OUT), .BUS_IN(DATA_BUS),
    .OUT({PCLATH, PC[12:8]}), .WREG_CLK_RST({WE, CLK_RST}), .WE_async(1'b0));  // open: AsynchronousW
  async_register async_register_5 (
    .SYNCH_ADDRESS(ADDRESS), .DIRECT_ADDRESS(7'b0001011), .BUS_OUT(DATA_BUS_OUT), .BUS_IN(DATA_BUS),
    .AsynchronousW(SFR_IN[7:0]), .OUT(SFR_OUT[23:16]), .WREG_CLK_RST({WE, CLK_RST}), .WE_async(Control_in[2]));
  assign controlled_buffer_2_out = WE ? DATA_BUS : 8'bz;  // Controlled_Buffer controlled_buffer_2
  RAM_part #(.addrWidth(7)) ram_1 (
    .addr(subtractor_1_out), .data(controlled_buffer_2_out), .sel(not_1_out), .clk(CLK_RST[0]),
    .ld(not_2_out), .clr(CLK_RST[1]));
  // Probe on controlled_buffer_2_out
  not not_2 (not_2_out, WE);
  // Probe on multiplexer_1_out
  // Probe on multiplexer_1_out
  assign DATA_BUS_OUT = not_3_out ? controlled_buffer_2_out : 8'bz;  // Controlled_Buffer controlled_buffer_3
  not not_3 (not_3_out, WE);
  not not_4 (not_4_out, SFR_OUT[15]);
  Multiplexer #(.width(7), .enable("false")) multiplexer_1 (
    .in0({7{1'b0}}), .in1(ADDRESS), .out(multiplexer_1_out), .sel(not_4_out));
  TIMR0 timr0_1 (
    .SYNCH_ADDRESS(multiplexer_1_out), .DIRECT_ADDRESS(7'b0000001), .BUS_OUT(DATA_BUS_OUT),
    .BUS_IN(DATA_BUS), .T0IF(TIMR0_ctrl[10]), .WREG_CLK_RST({WE, CLK_RST}), .RATE(Control_in[0]),
    .TIMR0(TIMR0_ctrl[7:0]));
  // Probe on TIMR0_ctrl[7:0]
  // Probe on porta_reg_1_out
  PORTA_reg porta_reg_1 (
    .BUS_IN(DATA_BUS), .SYNCH_ADDRESS(multiplexer_1_out), .DIRECT_ADDRESS(7'b0000101), .TRISA(TRISA),
    .BUS_OUT(DATA_BUS_OUT), .PIN_IN(IO[4:0]), .OUT(porta_reg_1_out), .WREG_CLK_RST({WE, CLK_RST}));
  // Probe on portb_reg_1_out
  PORTB_reg portb_reg_1 (
    .BUS_IN(DATA_BUS), .SYNCH_ADDRESS(multiplexer_1_out), .DIRECT_ADDRESS(7'b0000110), .TRISA(TRISB),
    .BUS_OUT(DATA_BUS_OUT), .RBIF(TIMR0_ctrl[8]), .PIN_IN(IO[12:5]), .OUT(portb_reg_1_out),
    .WREG_CLK_RST({WE, CLK_RST}));
  Comparator #(.width(7)) comparator_2 (.a(multiplexer_1_out), .b(7'b0000111), .eq(comparator_2_eq));  // open: gt, lt
  assign controlled_buffer_4_out = comparator_2_eq ? {8{1'b0}} : 8'bz;  // Controlled_Buffer controlled_buffer_4
  async_register async_register_6 (
    .SYNCH_ADDRESS(multiplexer_1_out), .DIRECT_ADDRESS(7'b0001000), .BUS_OUT(DATA_BUS_OUT),
    .BUS_IN(DATA_BUS), .OUT(EEPROM_in[15:8]), .WREG_CLK_RST({WE, CLK_RST}), .WE_async(1'b0));  // open: AsynchronousW
  // Probe on EEPROM_in[15:8]
  async_register async_register_7 (
    .SYNCH_ADDRESS(multiplexer_1_out), .DIRECT_ADDRESS(7'b0001001), .BUS_OUT(DATA_BUS_OUT),
    .BUS_IN(DATA_BUS), .AsynchronousW(EEDATA_in), .OUT(EEPROM_in[7:0]), .WREG_CLK_RST({WE, CLK_RST}),
    .WE_async(Control_in[3]));
  // Probe on EEPROM_in[7:0]
  assign DATA_BUS_OUT = controlled_buffer_4_out;  // Buffer buffer_2, 8 bits wide
  // Probe on multiplexer_2_out
  Multiplexer #(.width(7), .enable("false")) multiplexer_2 (
    .in0({7{1'b0}}), .in1(ADDRESS), .out(multiplexer_2_out), .sel(SFR_OUT[15]));
  // Probe on SFR_OUT[31:24]
  async_register async_register_8 (
    .SYNCH_ADDRESS(multiplexer_2_out), .DIRECT_ADDRESS(7'b0000001), .BUS_OUT(DATA_BUS_OUT),
    .BUS_IN(DATA_BUS), .OUT(SFR_OUT[31:24]), .WREG_CLK_RST({WE, CLK_RST}), .WE_async(1'b0));  // open: AsynchronousW
  async_register async_register_9 (
    .SYNCH_ADDRESS(multiplexer_2_out), .DIRECT_ADDRESS(7'b0000101), .BUS_OUT(DATA_BUS_OUT),
    .BUS_IN(DATA_BUS), .OUT(TRISA), .WREG_CLK_RST({WE, CLK_RST}), .WE_async(1'b0));  // open: AsynchronousW
  // Probe on TRISA
  // Probe on TRISB
  async_register async_register_10 (
    .SYNCH_ADDRESS(multiplexer_2_out), .DIRECT_ADDRESS(7'b0000110), .BUS_OUT(DATA_BUS),
    .BUS_IN(DATA_BUS_OUT), .OUT(TRISB), .WREG_CLK_RST({WE, CLK_RST}), .WE_async(1'b0));  // open: AsynchronousW
  Comparator #(.width(7)) comparator_3 (.a(multiplexer_2_out), .b(7'b0000111), .eq(comparator_3_eq));  // open: gt, lt
  assign controlled_buffer_5_out = comparator_3_eq ? {8{1'b0}} : 8'bz;  // Controlled_Buffer controlled_buffer_5
  async_register async_register_11 (
    .SYNCH_ADDRESS(multiplexer_2_out), .DIRECT_ADDRESS(7'b0001000), .BUS_OUT(DATA_BUS_OUT),
    .BUS_IN(DATA_BUS), .AsynchronousW(EEPROM_out[15:8]), .OUT(EEPROM_in[23:16]),
    .WREG_CLK_RST({WE, CLK_RST}), .WE_async(Control_in[3]));
  // Probe on EEPROM_in[23:16]
  assign DATA_BUS_OUT = controlled_buffer_5_out;  // Buffer buffer_3, 8 bits wide
  Button button_1 (.out(button_2_out[2]));
  Button button_2 (.out(button_2_out[0]));
  Clock clock_1 (.out(button_2_out[1]));

  assign {TIMR0_ctrl[11], TIMR0_ctrl[9]} = {Control_in[3], Control_in[4]};

  // Other names for the same wires on the sheet: TIMR_W = Control_in[0]; SW_E = Control_in[1]; INT_W = Control_in[2];
  //   EEIF = Control_in[3]; INTF = Control_in[4]; EEDATA[7:0] = EEPROM_in[7:0]; EEADR[7:0] = EEPROM_in[15:8];
  //   EECON1[7:0] = EEPROM_in[23:16]; EEDAT_in[7:0] = EEPROM_out[7:0]; EECON1_in[7:0] = EEPROM_out[15:8];
  //   PIN_A[4:0] = IO[4:0]; PIN_B[7:0] = IO[12:5]; PCL[7:0] = PC[7:0]; PCLATH[4:0] = PC[12:8];
  //   INT_IN[7:0] = SFR_IN[7:0]; SW[7:0] = SFR_IN[15:8]; FSR[7:0] = SFR_OUT[7:0]; STATUS[7:0] = SFR_OUT[15:8];
  //   RP0 = SFR_OUT[15]; INTCON[7:0] = SFR_OUT[23:16]; OPT[7:0] = SFR_OUT[31:24]; TIMR0[7:0] = TIMR0_ctrl[7:0];
  //   RBIF = TIMR0_ctrl[8]; T0IF = TIMR0_ctrl[10]

  // Notes on the sheet:
  //   PCL reg
  //   STATUS reg
  //   FSR reg
  //   PCLATH reg
  //   INTCON reg
  //   68x8
  //   RAM GFR
  //   TIMR0 reg
  //   PORTA reg
  //   PORTB reg
  //   EEADR reg
  //   EEDATA reg
  //   Bank 0
  //   EECON2
  //   OPTION reg
  //   TRISA reg
  //   TRISB reg
  //   EECON1 reg
  //   Bank 1
endmodule

module PORTA_reg (
  input  [2:0] WREG_CLK_RST,
  input  [7:0] BUS_IN,
  input  [6:0] SYNCH_ADDRESS,
  input  [6:0] DIRECT_ADDRESS,
  input  [7:0] TRISA,
  input  [4:0] PIN_IN,
  output [7:0] BUS_OUT,
  output [7:0] OUT
);

  wire and_1_out, comparator_1_eq, not_1_out;
  wire [7:0] controlled_buffer_1_out;

  Comparator #(.width(7)) comparator_1 (.a(SYNCH_ADDRESS), .b(DIRECT_ADDRESS), .eq(comparator_1_eq));  // open: gt, lt
  assign controlled_buffer_1_out = comparator_1_eq ? BUS_IN : 8'bz;  // Controlled_Buffer controlled_buffer_1
  not not_1 (not_1_out, WREG_CLK_RST[2]);
  and and_1 (and_1_out, comparator_1_eq, not_1_out);
  assign BUS_OUT = and_1_out ? {3'b000, OUT[4:0]} : 8'bz;  // Controlled_Buffer controlled_buffer_2
  PORT_reg port_reg_1 (
    .Data_Bus_In(controlled_buffer_1_out[0]), .WR_Port(WREG_CLK_RST[2]), .TRIS(TRISA[0]),
    .CLK(WREG_CLK_RST[0]), .I_O_pin(PIN_IN[0]), .I_O_pin_out(OUT[0]));
  PORT_reg port_reg_2 (
    .Data_Bus_In(controlled_buffer_1_out[1]), .WR_Port(WREG_CLK_RST[2]), .TRIS(TRISA[1]),
    .CLK(WREG_CLK_RST[0]), .I_O_pin(PIN_IN[1]), .I_O_pin_out(OUT[1]));
  PORT_reg port_reg_3 (
    .Data_Bus_In(controlled_buffer_1_out[2]), .WR_Port(WREG_CLK_RST[2]), .TRIS(TRISA[2]),
    .CLK(WREG_CLK_RST[0]), .I_O_pin(PIN_IN[2]), .I_O_pin_out(OUT[2]));
  PORT_reg port_reg_4 (
    .Data_Bus_In(controlled_buffer_1_out[3]), .WR_Port(WREG_CLK_RST[2]), .TRIS(TRISA[3]),
    .CLK(WREG_CLK_RST[0]), .I_O_pin(PIN_IN[3]), .I_O_pin_out(OUT[3]));
  PORT_reg port_reg_5 (
    .Data_Bus_In(controlled_buffer_1_out[4]), .WR_Port(WREG_CLK_RST[2]), .TRIS(TRISA[4]),
    .CLK(WREG_CLK_RST[0]), .I_O_pin(PIN_IN[4]), .I_O_pin_out(OUT[4]));

  assign OUT[7:5] = 3'b000;
endmodule

module PORTB_reg (
  input  [2:0] WREG_CLK_RST,
  input  [7:0] BUS_IN,
  input  [6:0] SYNCH_ADDRESS,
  input  [6:0] DIRECT_ADDRESS,
  input  [7:0] TRISA,
  input  [7:0] PIN_IN,
  output RBIF,
  output [7:0] BUS_OUT,
  output [7:0] OUT
);

  wire and_1_out, comparator_1_eq, not_1_out, port_reg_1_i_o_pin_out, port_reg_2_i_o_pin_out,
       port_reg_3_i_o_pin_out, port_reg_4_i_o_pin_out;
  wire [7:0] controlled_buffer_1_out;

  Comparator #(.width(7)) comparator_1 (.a(SYNCH_ADDRESS), .b(DIRECT_ADDRESS), .eq(comparator_1_eq));  // open: gt, lt
  Button button_1 ();  // open: out
  assign controlled_buffer_1_out = comparator_1_eq ? BUS_IN : 8'bz;  // Controlled_Buffer controlled_buffer_1
  not not_1 (not_1_out, WREG_CLK_RST[2]);
  and and_1 (and_1_out, comparator_1_eq, not_1_out);
  assign BUS_OUT = and_1_out ? OUT : 8'bz;  // Controlled_Buffer controlled_buffer_2
  Clock clock_1 ();  // open: out
  PORT_reg port_reg_1 (
    .Data_Bus_In(controlled_buffer_1_out[7]), .WR_Port(WREG_CLK_RST[2]), .TRIS(TRISA[7]),
    .CLK(WREG_CLK_RST[0]), .I_O_pin(PIN_IN[7]), .I_O_pin_out(port_reg_1_i_o_pin_out));
  PORT_reg port_reg_2 (
    .Data_Bus_In(controlled_buffer_1_out[6]), .WR_Port(WREG_CLK_RST[2]), .TRIS(TRISA[6]),
    .CLK(WREG_CLK_RST[0]), .I_O_pin(PIN_IN[6]), .I_O_pin_out(port_reg_2_i_o_pin_out));
  PORT_reg port_reg_3 (
    .Data_Bus_In(controlled_buffer_1_out[5]), .WR_Port(WREG_CLK_RST[2]), .TRIS(TRISA[5]),
    .CLK(WREG_CLK_RST[0]), .I_O_pin(PIN_IN[5]), .I_O_pin_out(port_reg_3_i_o_pin_out));
  PORT_reg port_reg_4 (
    .Data_Bus_In(controlled_buffer_1_out[4]), .WR_Port(WREG_CLK_RST[2]), .TRIS(TRISA[4]),
    .CLK(WREG_CLK_RST[0]), .I_O_pin(PIN_IN[4]), .I_O_pin_out(port_reg_4_i_o_pin_out));
  PORT_reg port_reg_5 (
    .Data_Bus_In(controlled_buffer_1_out[3]), .WR_Port(WREG_CLK_RST[2]), .TRIS(TRISA[3]),
    .CLK(WREG_CLK_RST[0]), .I_O_pin(PIN_IN[3]), .I_O_pin_out(OUT[3]));
  // PORT_reg port_reg_6: pin names not known; wires that end beside it: controlled_buffer_1_out[2], WREG_CLK_RST[2], TRISA[2], WREG_CLK_RST[0], PIN_IN[2], OUT[2]
  PORT_reg port_reg_7 (
    .Data_Bus_In(controlled_buffer_1_out[1]), .WR_Port(WREG_CLK_RST[2]), .TRIS(TRISA[1]),
    .CLK(WREG_CLK_RST[0]), .I_O_pin(PIN_IN[1]), .I_O_pin_out(OUT[1]));
  PORT_reg port_reg_8 (
    .Data_Bus_In(controlled_buffer_1_out[0]), .WR_Port(WREG_CLK_RST[2]), .TRIS(TRISA[0]),
    .CLK(WREG_CLK_RST[0]), .I_O_pin(PIN_IN[0]), .I_O_pin_out(OUT[0]));
  or or_1 (RBIF, port_reg_4_i_o_pin_out, port_reg_3_i_o_pin_out, port_reg_2_i_o_pin_out, port_reg_1_i_o_pin_out);
endmodule

module TIMR0 (
  input  [6:0] SYNCH_ADDRESS,
  input  [7:0] BUS_IN,
  input  [6:0] DIRECT_ADDRESS,
  input  [2:0] WREG_CLK_RST,
  input  RATE,
  output [7:0] BUS_OUT,
  output [7:0] TIMR0,
  output T0IF
);

  wire and_1_out, and_2_out, button_1_out, comparator_1_eq, not_1_out, not_2_out;
  wire [1:1] clock_1_out;

  not not_1 (not_1_out, WREG_CLK_RST[2]);
  Comparator #(.width(7)) comparator_1 (.a(SYNCH_ADDRESS), .b(DIRECT_ADDRESS), .eq(comparator_1_eq));  // open: gt, lt
  Clock clock_1 (.out(clock_1_out[1]));
  and and_1 (and_1_out, comparator_1_eq, not_1_out);
  and and_2 (and_2_out, comparator_1_eq, WREG_CLK_RST[2], not_2_out);
  not not_2 (not_2_out, RATE);
  Button button_1 (.out(button_1_out));
  assign BUS_OUT = and_1_out ? TIMR0 : 8'bz;  // Controlled_Buffer controlled_buffer_1
  Counter counter_1 (
    .load(and_2_out), .D(BUS_IN), .count(RATE), .Q(TIMR0), .carry(T0IF), .clk(WREG_CLK_RST[0]),
    .clr(WREG_CLK_RST[1]));
endmodule

module async_register (
  input  [6:0] SYNCH_ADDRESS,
  input  [7:0] BUS_IN,
  input  [7:0] AsynchronousW,
  input  [6:0] DIRECT_ADDRESS,
  input  [2:0] WREG_CLK_RST,
  input  WE_async,
  output [7:0] OUT,
  output [7:0] BUS_OUT
);

  wire and_1_out, and_2_out, comparator_1_eq, not_1_out, or_1_out;
  wire [7:0] DATA;

  Comparator #(.width(7)) comparator_1 (.a(SYNCH_ADDRESS), .b(DIRECT_ADDRESS), .eq(comparator_1_eq));  // open: gt, lt
  and and_1 (and_1_out, comparator_1_eq, WREG_CLK_RST[2]);
  and and_2 (and_2_out, comparator_1_eq, not_1_out);
  not not_1 (not_1_out, WREG_CLK_RST[2]);
  Register #(.trigger("high")) register_1 (
    .D(DATA), .en(or_1_out), .Q(OUT), .clk(WREG_CLK_RST[0]), .clr(WREG_CLK_RST[1]));
  or or_1 (or_1_out, and_1_out, WE_async);
  assign BUS_OUT = and_2_out ? OUT : 8'bz;  // Controlled_Buffer controlled_buffer_1
  Multiplexer #(.width(8), .enable("false")) multiplexer_1 (
    .in0(BUS_IN), .in1(AsynchronousW), .out(DATA), .sel(WE_async));
endmodule

module base_register (
  input  [7:0] D,
  input  EN,
  input  [1:0] CLK_RESET,
  output [7:0] Q
);

  Register #(.trigger("high")) register_1 (.D(D), .en(EN), .Q(Q), .clk(CLK_RESET[0]), .clr(CLK_RESET[1]));
endmodule

module PORT_reg (
  input  CLK,
  input  Data_Bus_In,
  input  I_O_pin,
  input  WR_Port,
  input  TRIS,
  output I_O_pin_out
);

  wire DATA_q, not_1_out;

  D_Flip_Flop DATA (.clk(CLK), .D(Data_Bus_In), .Q(DATA_q), .en(WR_Port));  // open: Qn, preset, reset
  assign I_O_pin_out = not_1_out ? DATA_q : 1'bz;  // Controlled_Buffer controlled_buffer_1
  not not_1 (not_1_out, TRIS);
  assign I_O_pin_out = TRIS ? I_O_pin : 1'bz;  // Controlled_Buffer controlled_buffer_2
endmodule

module PORT_change_reg (
  input  CLK,
  input  Data_Bus_In,
  input  I_O_pin,
  input  WR_Port,
  input  TRIS,
  output INT,
  output I_O_pin_out
);

  wire controlled_buffer_1_out, DATA_q, not_1_out, xor_1_out;

  D_Flip_Flop DATA (.clk(CLK), .D(Data_Bus_In), .Q(DATA_q), .en(WR_Port));  // open: Qn, preset, reset
  assign controlled_buffer_1_out = TRIS ? I_O_pin : 1'bz;  // Controlled_Buffer controlled_buffer_1
  assign controlled_buffer_1_out = not_1_out ? DATA_q : 1'bz;  // Controlled_Buffer controlled_buffer_2
  not not_1 (not_1_out, TRIS);
  D_Flip_Flop d_ff_1 (
    .clk(CLK), .D(controlled_buffer_1_out), .Q(I_O_pin_out), .en(xor_1_out));  // open: Qn, preset, reset
  and and_1 (INT, TRIS, controlled_buffer_1_out);
  xor xor_1 (xor_1_out, controlled_buffer_1_out, I_O_pin_out);
endmodule
