// Logisim project tty.circ as structural Verilog: 1 circuit, main circuit main
module main (
);

  wire and_2_out, CLKOUT, clr_2_out, clr_3_out, clr_4_out, clr_out, comparator_1_eq, MCLR_out, not_1_out,
       s_r_ff_1_q, s_r_ff_1_qn, undriven_2;
  wire [0:0] and_1_out;
  wire [4:0] pic16f84a_1_p6;
  wire [6:0] controlled_buffer_1_out, keyboard_1_data, Shift_reg_out, Shift_reg_q0, Shift_reg_q1,
       Shift_reg_q2, Shift_reg_q3, undriven;
  wire [7:0] multiplexer_1_out, multiplexer_2_out;
  wire [7:7] keyboard_1_avail, pic16f84a_1_p6_2;

  Keyboard #(.trigger("falling")) keyboard_1 (
    .clk(CLKOUT), .re(s_r_ff_1_qn), .clr(clr_out), .avail(keyboard_1_avail[7]), .data(keyboard_1_data));
  Button clr (.out(clr_out));
  and and_1 (and_1_out[0], s_r_ff_1_qn, keyboard_1_avail[7]);
  Multiplexer #(.width(8), .enable("false")) multiplexer_1 (
    .in0({keyboard_1_data, and_1_out[0]}), .in1({undriven, pic16f84a_1_p6[2]}), .out(multiplexer_1_out),
    .sel(pic16f84a_1_p6[2]));
  // Probe on multiplexer_1_out[7:1]
  TTY #(.trigger("falling")) tty_1 (
    .data(multiplexer_1_out[7:1]), .clk(CLKOUT), .we(multiplexer_1_out[0]), .clr(clr_2_out));
  Button clr_2 (.out(clr_2_out));
  // Probe on Shift_reg_q0
  Comparator #(.width(7)) comparator_1 (.a(7'b0001010), .b(Shift_reg_q0), .eq(comparator_1_eq));  // open: gt, lt
  Multiplexer #(.width(8), .enable("false")) multiplexer_2 (
    .in0({pic16f84a_1_p6_2[7], {7{1'b0}}}), .in1({keyboard_1_avail[7], keyboard_1_data}),
    .out(multiplexer_2_out), .sel(s_r_ff_1_qn));
  Shift_Register #(.width(7), .length(4), .trigger("falling")) Shift_reg (
    .shift(multiplexer_2_out[7]), .in(multiplexer_2_out[6:0]), .clk(CLKOUT), .out(Shift_reg_out),
    .clr(clr_3_out), .q0(Shift_reg_q0), .q1(Shift_reg_q1), .q2(Shift_reg_q2), .q3(Shift_reg_q3));  // open: load, d0, d1, d2, d3
  Button clr_3 (.out(clr_3_out));
  and and_2 (and_2_out, comparator_1_eq, not_1_out);
  not not_1 (not_1_out, pic16f84a_1_p6[3]);
  // Probe on Shift_reg_q3
  // Probe on Shift_reg_q0
  // Probe on Shift_reg_q2
  // Probe on Shift_reg_q1
  S_R_Flip_Flop s_r_ff_1 (
    .S(and_2_out), .clk(CLKOUT), .R(pic16f84a_1_p6[3]), .Q(s_r_ff_1_q), .Qn(s_r_ff_1_qn), .reset(clr_4_out));  // open: preset, en
  Button clr_4 (.out(clr_4_out));
  assign controlled_buffer_1_out = pic16f84a_1_p6_2[7] ? Shift_reg_out : 7'bz;  // Controlled_Buffer controlled_buffer_1
  Clock clock_1 ();  // open: out
  // Probe on pic16f84a_1_p6[3]
  Button button_1 ();  // open: out
  Button button_2 ();  // open: out
  // Probe on pic16f84a_1_p6_2[7]
  // Probe on s_r_ff_1_q
  // Probe on controlled_buffer_1_out
  // Probe on undriven
  // Probe on pic16f84a_1_p6[2]
  Button button_3 ();  // open: out
  Button MCLR (.out(MCLR_out));
  // Probe on undriven_2
  // PIC16F84A pic16f84a_1: pin names not known; wires that end beside it: MCLR_out, controlled_buffer_1_out[0], controlled_buffer_1_out[1], controlled_buffer_1_out[2], controlled_buffer_1_out[3], {pic16f84a_1_p6[4:2], pic16f84a_1_p6_2[7], pic16f84a_1_p6[0]}, CLKOUT, s_r_ff_1_q, controlled_buffer_1_out[6], controlled_buffer_1_out[5], controlled_buffer_1_out[4]

  // Notes on the sheet:
  //   keyboard
  //   enable write keyboard+shift to screen
  //   write  byte to PORTB
endmodule
