// Logisim project appolo181.circ as structural Verilog: 4 circuits, main circuit appolo181
module appolo181 (
);

  wire [1:0] clk_rst;
  wire [3:0] START_out;
  wire [5:0] undriven;
  wire [7:0] cpu_1_ram_address, ram_1_data;
  wire [11:0] rom_1_data;
  wire [23:0] counter_1_q;
  wire [31:0] DATA_STATES, INSTR_STATES;

  Button START (.out(START_out[0]));
  Button STOP (.out(START_out[1]));
  Button RESET (.out(START_out[2]));
  Clock clock_1 (.out(START_out[3]));
  CPU cpu_1 (
    .RAM_DATA(ram_1_data), .INPUTS({16{1'b1}}), .RAM_ADDRESS(cpu_1_ram_address), .COMMAND(START_out),
    .MACHINE_STATE(INSTR_STATES), .MACHINE_DATA(DATA_STATES), .out_4(clk_rst));
  RAM #(.bus("asynch")) ram_1 (.addr(cpu_1_ram_address), .data(ram_1_data));  // open: sel, ld, clr
  Counter #(.width(24), .max('hffffff)) counter_1 (
    .Q(counter_1_q), .clk(clk_rst[1]), .clr(clk_rst[0]));  // open: load, D, count, carry
  ROM #(.addrWidth(6), .dataWidth(12)) rom_1 (.addr(undriven), .data(rom_1_data));  // open: sel
  // Probe on rom_1_data
  RAM #(.addrWidth(24), .dataWidth(32), .bus("asynch")) ram_2 (
    .addr(counter_1_q), .data(INSTR_STATES), .ld(1'b0), .clr(clk_rst[0]));  // open: sel
  RAM #(.addrWidth(24), .dataWidth(32), .bus("asynch")) ram_3 (
    .addr(counter_1_q), .data(DATA_STATES), .ld(1'b0), .clr(clk_rst[0]));  // open: sel
  // Probe on INSTR_STATES
  // Probe on DATA_STATES

  // Notes on the sheet:
  //   Input
  //   Command
  //   Program
  //   contents of rom_1 (hex, n*v repeats v):
  //   a ab0 aaa 120 123 456
  //   Instruction state
  //   Data states
endmodule

module CPU (
  input  [15:0] INPUTS,
  input  [7:0] RAM_DATA,
  input  [3:0] COMMAND,
  output [1:0] out_4,
  output [7:0] RAM_ADDRESS,
  output [31:0] MACHINE_STATE,
  output [31:0] MACHINE_DATA
);

  wire acc_e, and_2_out, counter_1_carry, \end , jmp, jmp0, jmp_dbg, jmpIF, oe, or_1_out, reg_w, s_r_ff_1_q,
       sw_e;
  wire [0:0] counter_1_q;
  wire [1:0] dat_sel;
  wire [3:0] alu_1_status, alu_sel, OUTPUT, TEST;

  Button button_1 (.out(jmp_dbg));
  and and_1 (out_4[1], COMMAND[3], s_r_ff_1_q);
  S_R_Flip_Flop s_r_ff_1 (.Q(s_r_ff_1_q), .preset(COMMAND[0]), .reset(or_1_out));  // open: S, clk, R, Qn, en
  or or_1 (or_1_out, COMMAND[1], \end );
  Button START (.out(TEST[0]));
  Button STOP (.out(TEST[1]));
  Button RESET (.out(TEST[2]));
  Clock clock_1 (.out(TEST[3]));
  Counter #(.trigger("falling")) PC (
    .load(MACHINE_STATE[7]), .D(MACHINE_STATE[31:24]), .count(counter_1_carry), .Q(MACHINE_STATE[15:8]),
    .carry(\end ), .clk(out_4[1]), .clr(COMMAND[2]));
  Counter #(.width(1), .max('h1)) counter_1 (
    .Q(counter_1_q[0]), .carry(counter_1_carry), .clk(out_4[1]), .clr(COMMAND[2]));  // open: load, D, count
  or or_2 (jmp, jmp0, and_2_out);
  Multiplexer #(.width(8), .enable("false")) multiplexer_1 (
    .in0({8{1'b0}}), .in1({RAM_DATA[3:0], MACHINE_DATA[15:12]}), .out(MACHINE_STATE[31:24]), .sel(jmp_dbg));
  or or_3 (MACHINE_STATE[7], jmp_dbg, jmp);
  and and_2 (and_2_out, jmpIF, alu_1_status[0]);
  ROM #(.addrWidth(4), .dataWidth(4)) rom_1 ();  // open: addr, data, sel
  // Probe on alu_1_status
  // Probe on RAM_DATA
  ROM #(.addrWidth(5), .dataWidth(12)) rom_2 (
    .addr({RAM_DATA[7:4], counter_1_q[0]}), .data({alu_sel, jmpIF, jmp0, reg_w, sw_e, acc_e, oe, dat_sel}));  // open: sel
  Register #(.width(4)) register_1 (
    .D(MACHINE_DATA[3:0]), .en(acc_e), .Q(MACHINE_DATA[15:12]), .clk(out_4[1]), .clr(COMMAND[2]));
  // Probe on MACHINE_DATA[15:12]
  Register #(.width(4)) register_2 (
    .D(alu_1_status), .en(sw_e), .Q(MACHINE_DATA[11:8]), .clk(out_4[1]), .clr(COMMAND[2]));
  // Probe on MACHINE_DATA[7:4]
  // Probe on alu_sel
  // Probe on MACHINE_DATA[3:0]
  ALU alu_1 (
    .OUT(MACHINE_DATA[3:0]), .I1(MACHINE_DATA[15:12]), .I2(MACHINE_DATA[7:4]), .CB_IN(MACHINE_DATA[11:10]),
    .SEL(alu_sel), .STATUS(alu_1_status));
  Multiplexer #(.select(2), .width(4), .enable("false")) multiplexer_2 (
    .in0(INPUTS[3:0]), .in1(INPUTS[7:4]), .in2(INPUTS[11:8]), .in3(INPUTS[15:12]), .out(MACHINE_DATA[27:24]),
    .sel(RAM_DATA[1:0]));
  // Probe on MACHINE_DATA[23:20]
  // Probe on MACHINE_DATA[27:24]
  Multiplexer #(.select(2), .width(4), .disabled(0), .enable("false")) multiplexer_3 (
    .in0(MACHINE_DATA[27:24]), .in1(RAM_DATA[3:0]), .in2(MACHINE_DATA[23:20]), .out(MACHINE_DATA[7:4]),
    .sel(dat_sel));  // open: in3
  // Probe on MACHINE_DATA[7:4]
  _4bits_registersx4 u_4bits_registersx4_1 (
    .DATA(MACHINE_DATA[15:12]), .ADDR(RAM_DATA[1:0]), .CLK_RESET({out_4[1], COMMAND[2]}), .W(reg_w),
    .OUT(MACHINE_DATA[23:20]));
  _4bits_registersx4 u_4bits_registersx4_2 (
    .DATA(MACHINE_DATA[15:12]), .ADDR(RAM_DATA[1:0]), .CLK_RESET({out_4[1], COMMAND[2]}), .W(oe), .OUT(OUTPUT));

  assign {MACHINE_DATA[31:28], MACHINE_DATA[19:16]} = {4'b0000, RAM_DATA[3:0]};
  assign {MACHINE_STATE[23:16], MACHINE_STATE[6:0]} = {RAM_DATA, {7{1'b0}}};
  assign out_4[0] = COMMAND[2];
  assign RAM_ADDRESS = MACHINE_STATE[15:8];

  // Other names for the same wires on the sheet: clk_rst[1:0] = {out_4[1], COMMAND[2]}; rst = COMMAND[2];
  //   start = COMMAND[0]; stop = COMMAND[1]; clk = COMMAND[3]; RESULT[3:0] = MACHINE_DATA[3:0];
  //   DATA_BUS[3:0] = MACHINE_DATA[7:4]; SW[3:0] = MACHINE_DATA[11:8]; ACCU[3:0] = MACHINE_DATA[15:12];
  //   DATA[3:0] = RAM_DATA[3:0]; INSTRUCTION[7:0] = RAM_DATA; REG[3:0] = MACHINE_DATA[23:20];
  //   INPUT[3:0] = MACHINE_DATA[27:24]; jump = MACHINE_STATE[7]; RAMaddress[7:0] = MACHINE_STATE[15:8];
  //   OPCODE[3:0] = RAM_DATA[7:4]; JUMP_ADDRESS[7:0] = MACHINE_STATE[31:24]

  // Notes on the sheet:
  //   Start/Stop unit
  //   Jump managment
  //   Instruction Control
  //   Program counter
  //   PROM
  //   Jump and ALU
  //   contents of rom_2 (hex, n*v repeats v):
  //   0 0 100 4*0 20 1 21 1 81 11 31 20 30 1 51 0 50 2 22 0 5
  //   Data Managment
  //   Bus selection
  //   Outputs
endmodule

module _4bits_registersx4 (
  input  [3:0] DATA,
  input  [1:0] ADDR,
  input  [1:0] CLK_RESET,
  input  W,
  output [3:0] OUT
);

  wire decoder_1_out0, decoder_1_out1, decoder_1_out2, decoder_1_out3;
  wire [3:0] register_1_q, register_2_q, register_3_q, register_4_q;

  Decoder #(.select(2), .disabled(0)) decoder_1 (
    .out0(decoder_1_out0), .out1(decoder_1_out1), .out2(decoder_1_out2), .out3(decoder_1_out3), .sel(ADDR),
    .en(W));
  Register #(.width(4), .trigger("high")) register_1 (
    .D(DATA), .en(decoder_1_out3), .Q(register_1_q), .clk(CLK_RESET[1]), .clr(CLK_RESET[0]));
  Register #(.width(4), .trigger("high")) register_2 (
    .D(DATA), .en(decoder_1_out2), .Q(register_2_q), .clk(CLK_RESET[1]), .clr(CLK_RESET[0]));
  Register #(.width(4), .trigger("high")) register_3 (
    .D(DATA), .en(decoder_1_out1), .Q(register_3_q), .clk(CLK_RESET[1]), .clr(CLK_RESET[0]));
  Multiplexer #(.select(2), .width(4), .enable("false")) multiplexer_1 (
    .in0(register_1_q), .in1(register_2_q), .in2(register_3_q), .in3(register_4_q), .out(OUT), .sel(ADDR));
  Register #(.width(4), .trigger("high")) register_4 (
    .D(DATA), .en(decoder_1_out0), .Q(register_4_q), .clk(CLK_RESET[1]), .clr(CLK_RESET[0]));
endmodule

module ALU (
  input  [3:0] I1,
  input  [3:0] I2,
  input  [1:0] CB_IN,
  input  [3:0] SEL,
  output [3:0] OUT,
  output [3:0] STATUS
);

  wire [3:0] adder_1_out, and_1_out, buffer_1_out, not_1_out, or_1_out, shifter_1_out, shifter_2_out,
       subtractor_1_out, xor_1_out;

  Comparator #(.width(4)) comparator_1 (.a(I2), .b(I1), .gt(STATUS[1]), .eq(STATUS[0]));  // open: lt
  Adder #(.width(4)) adder_1 (.a(I2), .b(I1), .out(adder_1_out), .cin(CB_IN[0]), .cout(STATUS[2]));
  Subtractor #(.width(4)) subtractor_1 (.a(I2), .b(I1), .out(subtractor_1_out), .bin(CB_IN[1]), .bout(STATUS[3]));
  assign and_1_out = I1 & I2;  // AND_Gate and_1, 4 bits wide
  assign or_1_out = I1 | I2;  // OR_Gate or_1, 4 bits wide
  assign not_1_out = ~I1;  // NOT_Gate not_1, 4 bits wide
  assign xor_1_out = I1 ^ I2;  // XOR_Gate xor_1, 4 bits wide
  assign buffer_1_out = I1;  // Buffer buffer_1, 4 bits wide
  Shifter #(.width(4), .shift("rl")) shifter_1 (.in(I1), .\dist ({1'b0, CB_IN[0]}), .out(shifter_1_out));
  Shifter #(.width(4), .shift("rl")) shifter_2 (.in(I2), .\dist ({1'b0, CB_IN[0]}), .out(shifter_2_out));
  Multiplexer #(.select(4), .width(4), .enable("false")) multiplexer_1 (
    .in0(shifter_2_out), .in1(shifter_1_out), .in2(buffer_1_out), .in3(not_1_out), .in4(xor_1_out),
    .in5(or_1_out), .in6(and_1_out), .in7(subtractor_1_out), .in8(adder_1_out), .out(OUT), .sel(SEL));  // open: in9, in10, in11, in12, in13, in14, in15
endmodule
